# Fritzing sketch mors-sketch (saved by Fritzing 0.9.3b)
breadboards: 1

parts:
  R1 = Rotary Potentiometer (Small) [maximum_resistance=100kΩ package=THT]
  LCD1 = LCD screen
  J1 = Piezo Speaker
  Parça1 = Arduino Uno (Rev3)
  hc-sr1 = hc-sr04
  S1 = Pushbutton [package="[THT]"]
  R2 = Resistor [tolerance=±5% resistance=220 package="1206 [SMD]"]
  R3 = Resistor [tolerance=±5% resistance=220 package="1206 [SMD]"]
  S2 = Pushbutton [package="[THT]"]
  R4 = Resistor [tolerance=±5% resistance=220 package="1206 [SMD]"]

nets:
  VDD: R1.leg1, LCD1.VDD, Parça1.5V, hc-sr1.VCC, S1.Pin_3, S1.Pin_4, S2.Pin_3, S2.Pin_4, R4.Pin_1
  N1: R1.wiper, LCD1.V0
  GND: R1.leg2, LCD1.VSS, LCD1.R/W, LCD1.LED-, J1.pin1, Parça1.GND, hc-sr1.GND, R2.Pin_1, R3.Pin_1
  N2: LCD1.RS, Parça1.D12/MISO
  N3: LCD1.E, Parça1.D11_PWM/MOSI
  N4: LCD1.DB4, Parça1.D5_PWM
  N5: LCD1.DB5, Parça1.D4
  N6: LCD1.DB6, Parça1.D3_PWM
  N7: LCD1.DB7, Parça1.D2
  N8: LCD1.LED+, R4.Pin_0
  N9: J1.pin2, Parça1.D8
  N10: Parça1.D9_PWM, hc-sr1.Echo
  N11: Parça1.D10_PWM/SS, hc-sr1.Trig
  N12: Parça1.D6_PWM, S1.Pin_1, S1.Pin_2, R3.Pin_0
  N13: Parça1.D7, R2.Pin_0, S2.Pin_1, S2.Pin_2
